# Fritzing sketch ZenS (saved by Fritzing 0.9.3b)
breadboards: 1

parts:
  Mega = Arduino Mega 2560 (Rev3)
  SD_R\Wer = microSD Socket [package="Molex 502774-0891 [SMD]"]
  IR = LTE-302 [package=lte-302]
  Lithium_battery = Battery
  LedC = LED - 5mm [color="Red (633nm)" package="5 mm [THT]"]  # not connected
  LedB = LED - 5mm [color="Red (633nm)" package="5 mm [THT]"]  # not connected
  LedA = LED - 5mm [color="Red (633nm)" package="5 mm [THT]"]
  LedD = LED - 5mm [color="Red (633nm)" package="5 mm [THT]"]  # not connected
  ButtonA = Pushbutton [package=THT]  # not connected
  ButtonB = Pushbutton [package=THT]
  ButtonC = Pushbutton [package=THT]
  ButtonD = Pushbutton [package=THT]
  JY61 = IC, DIP package, 8 pins [chip_label=IC]
  Battery_Button = Pushbutton [package=THT]
  Charge_and_discharge_integrated_module = PowerBoost 500 Charger
  R1 = Resistor [tolerance=±5% resistance=220 package=THT]
  R2 = Resistor [tolerance=±5% resistance=220 package=THT]
  Power_plug = Power plug

nets:
  GND: Mega.GND, JY61.pin1, Battery_Button.leg1, Charge_and_discharge_integrated_module.GND, R1.Pin_0, R2.Pin_1
  N1: Mega.D10_PWM, JY61.pin3
  N2: Mega.D9_PWM, JY61.pin2
  5V: Mega.5V, SD_R\Wer.VCC, IR.A, ButtonB.leg1, ButtonC.leg1, ButtonD.leg1, JY61.pin4, R1.Pin_1
  N3: Mega.VIN, Charge_and_discharge_integrated_module.5.0V
  N4: Mega.D50, SD_R\Wer.DO
  N5: Mega.D51, SD_R\Wer.DI
  N6: Mega.D52, SD_R\Wer.SCK
  N7: Mega.D53, SD_R\Wer.CS
  N8: Lithium_battery.-, Charge_and_discharge_integrated_module.VBAT_OUT
  N9: Lithium_battery.+, Charge_and_discharge_integrated_module.VBAT_IN
  N10: LedA.cathode, R2.Pin_0
  N11: Charge_and_discharge_integrated_module.GND_BAT_IN, Power_plug.GND
  N12: Charge_and_discharge_integrated_module.USB, Power_plug.VCC

notes:
  元件代替表：
  MicroSD Socket 去掉:NC,RSV,SHIELD
  JY61(加计\陀螺仪\角速度计):对应IC, 1-VCC, 2-RX, 3-TX, 4-GND
  Charge and discharge integrated module: 对应Power Boost 500Charger, VBAT OUT-GND, VBAT IN-BAT, USB-IN, 5.0V-VCC, GND-GND, GND VBAT IN -GND, ENABLE-KEY, 去掉LBO
